// Logisim project hw4.circ as structural Verilog: 17 circuits, main circuit main
module main (
  input  reset
);

  wire add, addi, alu_1_out_8, alu_1_out_9, \and , and_1_out, and_2_out, beq, bit12, bit13, bit14, bit15,
       blt, clk, datamemWE, \input , j, jal, keyboard_1_avail, Lshift, lw, memory_latch_1_oe_latched,
       memory_latch_1_we_latched, not_1_out, not_2_out, not_4_out, NovalidData, \or , or_3_out, \output ,
       regfileWE, sALU0, sALU1, selectALUin, selectALUsub, selectJump, selectRd, shr, sub, subi;
  wire [2:0] multiplexer_2_out, multiplexer_3_out;
  wire [6:0] keyboardData;
  wire [11:0] currentPC;
  wire [15:0] address, alu_1_output, keyInput, memory_latch_1_address_latched,
       memory_latch_1_data_in_latched, multiplexer_4_out, multiplexer_5_out, multiplexer_6_out,
       multiplexer_7_out, multiplexer_8_out, multiplexer_9_out, pcPlusOne, ram_1_dout, registerfile_1_rtout,
       RsVal, signextender_1_out_2, sixteenbitadder_2_result;

  Clock clock_1 (.out(clk));
  not not_1 (not_1_out, clk);
  TTY #(.rows(13), .cols(80), .trigger("falling")) tty_1 (.data(RsVal[6:0]), .clk(clk), .we(\output ), .clr(reset));
  sixteenBitRegister PC (
    .in_1(multiplexer_6_out), .in_2(not_2_out), .in_3(reset), .out_5({address[15:12], currentPC}), .in_4(1'b1));
  not not_2 (not_2_out, not_1_out);
  Keyboard keyboard_1 (.clk(clk), .re(\input ), .clr(reset), .avail(keyboard_1_avail), .data(keyboardData));
  not not_3 (NovalidData, keyboard_1_avail);
  ROM #(.addrWidth(16), .dataWidth(16)) rom_1 (
    .addr({address[15:12], currentPC}), .data({bit15, bit14, bit13, bit12, address[11:0]}));
  Multiplexer #(.width(16), .enable("false")) multiplexer_1 (
    .in0({{9{1'b0}}, keyboardData}), .in1(16'h80), .out(keyInput), .sel(NovalidData));
  sixteenBitAdder sixteenbitadder_1 (
    .sub(1'b0), .result(pcPlusOne), .B(16'h1), .A({address[15:12], currentPC}));  // open: ovf, zero, out_7
  not not_4 (not_4_out, clk);
  Multiplexer #(.width(3), .enable("false")) multiplexer_2 (
    .in0(multiplexer_3_out), .in1(3'b111), .out(multiplexer_2_out), .sel(jal));
  Multiplexer #(.width(3), .enable("false")) multiplexer_3 (
    .in0(address[8:6]), .in1(address[5:3]), .out(multiplexer_3_out), .sel(selectRd));
  RegisterFile registerfile_1 (
    .in_1(not_4_out), .in_3(regfileWE), .in_4(reset), .Rs(address[11:9]), .inputData(multiplexer_9_out),
    .rsout(RsVal), .rtout(registerfile_1_rtout), .Rt(address[8:6]), .Rd(multiplexer_2_out));
  Decoder #(.select(4)) decoder_1 (
    .out0(lw), .out1(datamemWE), .out2(beq), .out3(blt), .out4(\or ), .out5(\and ), .out6(addi), .out7(add),
    .out8(sub), .out9(subi), .out10(shr), .out11(Lshift), .out12(j), .out13(jal), .out14(\output ),
    .out15(\input ), .sel({bit15, bit14, bit13, bit12}), .en(1'b1));
  signExtender signextender_1 (.in_1(address[5:0]), .out_2(signextender_1_out_2));
  sixteenBitAdder sixteenbitadder_2 (
    .sub(1'b0), .result(sixteenbitadder_2_result), .B(signextender_1_out_2), .A(pcPlusOne));  // open: ovf, zero, out_7
  Multiplexer #(.width(16), .enable("false")) multiplexer_4 (
    .in0(registerfile_1_rtout), .in1(signextender_1_out_2), .out(multiplexer_4_out), .sel(selectALUin));
  or or_1 (regfileWE, lw, \or , \and , addi, add, sub, subi, shr, Lshift, jal, \input );
  memory_latch memory_latch_1 (
    .address(alu_1_output), .WE(datamemWE), .clk(clk), .data_in(registerfile_1_rtout),
    .address_latched(memory_latch_1_address_latched), .WE_latched(memory_latch_1_we_latched),
    .OE_latched(memory_latch_1_oe_latched), .data_in_latched(memory_latch_1_data_in_latched));
  alu alu_1 (
    .select({sALU1, sALU0}), .input1(RsVal), .input2(multiplexer_4_out), .\output (alu_1_output),
    .in_4(selectALUsub), .out_9(alu_1_out_9), .in_5(address[2:0]), .in_6(Lshift), .out_8(alu_1_out_8));
  or or_2 (selectRd, \or , \and , add, sub, shr, Lshift, \input );
  Multiplexer #(.width(16), .enable("false")) multiplexer_5 (
    .in0(pcPlusOne), .in1(sixteenbitadder_2_result), .out(multiplexer_5_out), .sel(or_3_out));
  and and_1 (and_1_out, beq, alu_1_out_9);
  or or_3 (or_3_out, and_1_out, and_2_out);
  and and_2 (and_2_out, blt, alu_1_out_8);
  or or_4 (selectJump, jal, j);
  Multiplexer #(.width(16), .enable("false")) multiplexer_6 (
    .in0(multiplexer_5_out), .in1(address), .out(multiplexer_6_out), .sel(selectJump));
  or or_5 (selectALUin, addi, subi, datamemWE, lw);
  RAM #(.addrWidth(16), .dataWidth(16), .trigger("high"), .databus("bibus")) ram_1 (
    .addr(memory_latch_1_address_latched), .we(memory_latch_1_we_latched), .oe(memory_latch_1_oe_latched),
    .din(memory_latch_1_data_in_latched), .dout(ram_1_dout));
  or or_6 (sALU1, \and , Lshift, shr);
  or or_7 (selectALUsub, beq, blt, subi, sub);
  or or_8 (sALU0, \or , Lshift, shr);
  Multiplexer #(.width(16), .enable("false")) multiplexer_7 (
    .in0(alu_1_output), .in1(ram_1_dout), .out(multiplexer_7_out), .sel(lw));
  Multiplexer #(.width(16), .enable("false")) multiplexer_8 (
    .in0(multiplexer_7_out), .in1(pcPlusOne), .out(multiplexer_8_out), .sel(jal));
  Multiplexer #(.width(16), .enable("false")) multiplexer_9 (
    .in0(multiplexer_8_out), .in1(keyInput), .out(multiplexer_9_out), .sel(\input ));

  // Other names for the same wires on the sheet: bit0 = address[0]; immediate[5:0] = address[5:0];
  //   shamt[2:0] = address[2:0]; bit1 = address[1]; bit2 = address[2]; bit3 = address[3]; rd[2:0] = address[5:3];
  //   bit4 = address[4]; bit5 = address[5]; bit6 = address[6]; rt[2:0] = address[8:6]; bit7 = address[7];
  //   bit8 = address[8]; bit9 = address[9]; rs[2:0] = address[11:9]; bit10 = address[10]; bit11 = address[11];
  //   currentPC[15:12] = address[15:12]; pcBit12 = address[12]; pcBit13 = address[13]; pcBit14 = address[14];
  //   pcBit15 = address[15]; keyboardVal[6:0] = keyboardData; opcode[3:0] = {bit15, bit14, bit13, bit12};
  //   selectBeq = beq; selectBlt = blt; selectInput = \input ; selectJal = jal; selectRegfileIn = lw;
  //   selectTTY = \output ; shl = Lshift; sw = datamemWE
endmodule

module sixteenBitRegister (
  input  [15:0] in_1,
  input  in_2,
  input  in_3,
  input  in_4,
  output [15:0] out_5
);

  wire and_1_out;

  and and_1 (and_1_out, in_2, in_4);
  D_Flip_Flop d_ff_1 (.D(in_1[0]), .clk(and_1_out), .Q(out_5[0]), .reset(in_3));  // open: Qn, preset
  D_Flip_Flop d_ff_2 (.D(in_1[1]), .clk(and_1_out), .Q(out_5[1]), .reset(in_3));  // open: Qn, preset
  D_Flip_Flop d_ff_3 (.D(in_1[2]), .clk(and_1_out), .Q(out_5[2]), .reset(in_3));  // open: Qn, preset
  D_Flip_Flop d_ff_4 (.D(in_1[3]), .clk(and_1_out), .Q(out_5[3]), .reset(in_3));  // open: Qn, preset
  D_Flip_Flop d_ff_5 (.D(in_1[4]), .clk(and_1_out), .Q(out_5[4]), .reset(in_3));  // open: Qn, preset
  D_Flip_Flop d_ff_6 (.D(in_1[5]), .clk(and_1_out), .Q(out_5[5]), .reset(in_3));  // open: Qn, preset
  D_Flip_Flop d_ff_7 (.D(in_1[6]), .clk(and_1_out), .Q(out_5[6]), .reset(in_3));  // open: Qn, preset
  D_Flip_Flop d_ff_8 (.D(in_1[7]), .clk(and_1_out), .Q(out_5[7]), .reset(in_3));  // open: Qn, preset
  D_Flip_Flop d_ff_9 (.D(in_1[8]), .clk(and_1_out), .Q(out_5[8]), .reset(in_3));  // open: Qn, preset
  D_Flip_Flop d_ff_10 (.D(in_1[9]), .clk(and_1_out), .Q(out_5[9]), .reset(in_3));  // open: Qn, preset
  D_Flip_Flop d_ff_11 (.D(in_1[10]), .clk(and_1_out), .Q(out_5[10]), .reset(in_3));  // open: Qn, preset
  D_Flip_Flop d_ff_12 (.D(in_1[11]), .clk(and_1_out), .Q(out_5[11]), .reset(in_3));  // open: Qn, preset
  D_Flip_Flop d_ff_13 (.D(in_1[12]), .clk(and_1_out), .Q(out_5[12]), .reset(in_3));  // open: Qn, preset
  D_Flip_Flop d_ff_14 (.D(in_1[13]), .clk(and_1_out), .Q(out_5[13]), .reset(in_3));  // open: Qn, preset
  D_Flip_Flop d_ff_15 (.D(in_1[14]), .clk(and_1_out), .Q(out_5[14]), .reset(in_3));  // open: Qn, preset
  D_Flip_Flop d_ff_16 (.D(in_1[15]), .clk(and_1_out), .Q(out_5[15]), .reset(in_3));  // open: Qn, preset

  // Other names for the same wires on the sheet: clk = in_2; bit0 = in_1[0]; bit1 = in_1[1]; bit2 = in_1[2];
  //   bit3 = in_1[3]; bit4 = in_1[4]; bit5 = in_1[5]; bit6 = in_1[6]; bit7 = in_1[7]; bit8 = in_1[8]; bit9 = in_1[9];
  //   bit10 = in_1[10]; bit11 = in_1[11]; bit12 = in_1[12]; bit13 = in_1[13]; bit14 = in_1[14]; bit15 = in_1[15];
  //   out0 = out_5[0]; out1 = out_5[1]; out2 = out_5[2]; out3 = out_5[3]; out4 = out_5[4]; out5 = out_5[5];
  //   out6 = out_5[6]; out7 = out_5[7]; out8 = out_5[8]; out9 = out_5[9]; out10 = out_5[10]; out11 = out_5[11];
  //   out12 = out_5[12]; out13 = out_5[13]; out14 = out_5[14]; out15 = out_5[15]; regWE = in_4; reset = in_3
endmodule

module RegisterFile (
  input  in_1,
  input  [15:0] inputData,
  input  in_3,
  input  in_4,
  input  [2:0] Rs,
  input  [2:0] Rt,
  input  [2:0] Rd,
  output [15:0] rsout,
  output [15:0] rtout
);

  wire and_1_out, and_2_out, and_3_out, and_4_out, and_5_out, and_6_out, and_7_out, and_8_out, Rd0, Rd1, Rd2,
       Rd3, Rd4, Rd5, Rd6, Rd7, Rs0, Rs1, Rs2, Rs3, Rs4, Rs5, Rs6, Rs7, Rt0, Rt1, Rt2, Rt3, Rt4, Rt5, Rt6,
       Rt7;
  wire [15:0] sixteenbitregister_1_out_5, sixteenbitregister_2_out_5, sixteenbitregister_3_out_5,
       sixteenbitregister_4_out_5, sixteenbitregister_5_out_5, sixteenbitregister_6_out_5,
       sixteenbitregister_7_out_5, sixteenbitregister_8_out_5;

  Decoder #(.select(3)) decoder_1 (
    .out0(Rs0), .out1(Rs1), .out2(Rs2), .out3(Rs3), .out4(Rs4), .out5(Rs5), .out6(Rs6), .out7(Rs7), .sel(Rs),
    .en(1'b1));
  Decoder #(.select(3)) decoder_2 (
    .out0(Rt0), .out1(Rt1), .out2(Rt2), .out3(Rt3), .out4(Rt4), .out5(Rt5), .out6(Rt6), .out7(Rt7), .sel(Rt),
    .en(1'b1));
  Decoder #(.select(3)) decoder_3 (
    .out0(Rd0), .out1(Rd1), .out2(Rd2), .out3(Rd3), .out4(Rd4), .out5(Rd5), .out6(Rd6), .out7(Rd7), .sel(Rd),
    .en(1'b1));
  sixteenBitRegister sixteenbitregister_1 (
    .in_1({16{1'b0}}), .in_2(in_1), .in_3(in_4), .out_5(sixteenbitregister_1_out_5), .in_4(and_1_out));
  and and_1 (and_1_out, in_3, Rd0);
  sixteenBitRegister sixteenbitregister_2 (
    .in_1(inputData), .in_2(in_1), .in_3(in_4), .out_5(sixteenbitregister_2_out_5), .in_4(and_2_out));
  and and_2 (and_2_out, in_3, Rd1);
  sixteenBitRegister sixteenbitregister_3 (
    .in_1(inputData), .in_2(in_1), .in_3(in_4), .out_5(sixteenbitregister_3_out_5), .in_4(and_3_out));
  and and_3 (and_3_out, in_3, Rd2);
  sixteenBitRegister sixteenbitregister_4 (
    .in_1(inputData), .in_2(in_1), .in_3(in_4), .out_5(sixteenbitregister_4_out_5), .in_4(and_4_out));
  and and_4 (and_4_out, in_3, Rd3);
  sixteenBitRegister sixteenbitregister_5 (
    .in_1(inputData), .in_2(in_1), .in_3(in_4), .out_5(sixteenbitregister_5_out_5), .in_4(and_5_out));
  and and_5 (and_5_out, in_3, Rd4);
  sixteenBitRegister sixteenbitregister_6 (
    .in_1(inputData), .in_2(in_1), .in_3(in_4), .out_5(sixteenbitregister_6_out_5), .in_4(and_6_out));
  and and_6 (and_6_out, in_3, Rd5);
  sixteenBitRegister sixteenbitregister_7 (
    .in_1(inputData), .in_2(in_1), .in_3(in_4), .out_5(sixteenbitregister_7_out_5), .in_4(and_7_out));
  and and_7 (and_7_out, in_3, Rd6);
  sixteenBitRegister sixteenbitregister_8 (
    .in_1(inputData), .in_2(in_1), .in_3(in_4), .out_5(sixteenbitregister_8_out_5), .in_4(and_8_out));
  and and_8 (and_8_out, in_3, Rd7);
  // Probe on sixteenbitregister_1_out_5
  // Probe on sixteenbitregister_2_out_5
  // Probe on sixteenbitregister_3_out_5
  // Probe on sixteenbitregister_4_out_5
  // Probe on sixteenbitregister_5_out_5
  // Probe on sixteenbitregister_6_out_5
  // Probe on sixteenbitregister_7_out_5
  // Probe on sixteenbitregister_8_out_5
  assign rsout = Rs0 ? sixteenbitregister_1_out_5 : 16'bz;  // Controlled_Buffer controlled_buffer_1
  assign rtout = Rt0 ? sixteenbitregister_1_out_5 : 16'bz;  // Controlled_Buffer controlled_buffer_2
  assign rsout = Rs1 ? sixteenbitregister_2_out_5 : 16'bz;  // Controlled_Buffer controlled_buffer_3
  assign rtout = Rt1 ? sixteenbitregister_2_out_5 : 16'bz;  // Controlled_Buffer controlled_buffer_4
  assign rsout = Rs2 ? sixteenbitregister_3_out_5 : 16'bz;  // Controlled_Buffer controlled_buffer_5
  assign rtout = Rt2 ? sixteenbitregister_3_out_5 : 16'bz;  // Controlled_Buffer controlled_buffer_6
  assign rsout = Rs3 ? sixteenbitregister_4_out_5 : 16'bz;  // Controlled_Buffer controlled_buffer_7
  assign rtout = Rt3 ? sixteenbitregister_4_out_5 : 16'bz;  // Controlled_Buffer controlled_buffer_8
  assign rsout = Rs4 ? sixteenbitregister_5_out_5 : 16'bz;  // Controlled_Buffer controlled_buffer_9
  assign rtout = Rt4 ? sixteenbitregister_5_out_5 : 16'bz;  // Controlled_Buffer controlled_buffer_10
  assign rsout = Rs5 ? sixteenbitregister_6_out_5 : 16'bz;  // Controlled_Buffer controlled_buffer_11
  assign rtout = Rt5 ? sixteenbitregister_6_out_5 : 16'bz;  // Controlled_Buffer controlled_buffer_12
  assign rsout = Rs6 ? sixteenbitregister_7_out_5 : 16'bz;  // Controlled_Buffer controlled_buffer_13
  assign rtout = Rt6 ? sixteenbitregister_7_out_5 : 16'bz;  // Controlled_Buffer controlled_buffer_14
  assign rsout = Rs7 ? sixteenbitregister_8_out_5 : 16'bz;  // Controlled_Buffer controlled_buffer_15
  assign rtout = Rt7 ? sixteenbitregister_8_out_5 : 16'bz;  // Controlled_Buffer controlled_buffer_16

  // Other names for the same wires on the sheet: clk = in_1; input[15:0] = inputData; reset = in_4; WE = in_3
endmodule

module alu (
  input  [1:0] select,
  input  [15:0] input1,
  input  [15:0] input2,
  input  in_4,
  input  [2:0] in_5,
  input  in_6,
  output [15:0] \output ,
  output out_8,
  output out_9
);

  wire [15:0] adder, \and , Lshift, multiplexer_1_out, \not , \or , Rshift;

  rightBarrelshifter rightbarrelshifter_1 (.shiftBits(in_5), .in_2(input1), .out_3(Rshift));
  leftBarrelshifter leftbarrelshifter_1 (.shiftBits(in_5), .in_2(input1), .out_3(Lshift));
  sixteenBitAdder sixteenbitadder_1 (
    .sub(in_4), .result(adder), .B(input2), .A(input1), .zero(out_9), .out_7(out_8));  // open: ovf
  assign \or  = input1 | input2;  // OR_Gate or_1, 16 bits wide
  assign \and  = input1 & input2;  // AND_Gate and_1, 16 bits wide
  assign \not  = ~input1;  // NOT_Gate not_1, 16 bits wide
  Multiplexer #(.width(16), .enable("false")) multiplexer_1 (
    .in0(Rshift), .in1(Lshift), .out(multiplexer_1_out), .sel(in_6));
  Multiplexer #(.select(2), .width(16), .enable("false")) multiplexer_2 (
    .in0(adder), .in1(\or ), .in2(\and ), .in3(multiplexer_1_out), .out(\output ), .sel(select));

  // Other names for the same wires on the sheet: leftShift = in_6; shiftBit[2:0] = in_5; subBit = in_4
endmodule

module oneBitAdder (
  input  sub,
  input  A,
  input  B,
  output result,
  output ovf
);

  wire and_1_out, and_2_out, xor_1_out;

  and and_1 (and_1_out, B, A);
  or or_1 (ovf, and_1_out, and_2_out);
  xor xor_1 (xor_1_out, A, B);
  and and_2 (and_2_out, xor_1_out, sub);
  xor xor_2 (result, sub, xor_1_out);
endmodule

module sixteenBitAdder (
  input  [15:0] B,
  input  sub,
  input  [15:0] A,
  output ovf,
  output [15:0] result,
  output zero,
  output out_7
);

  wire onebitadder_1_ovf, onebitadder_2_ovf, onebitadder_3_ovf, onebitadder_4_ovf, onebitadder_5_ovf,
       onebitadder_6_ovf, onebitadder_7_ovf, onebitadder_8_ovf, onebitadder_9_ovf, onebitadder_10_ovf,
       onebitadder_11_ovf, onebitadder_12_ovf, onebitadder_13_ovf, onebitadder_14_ovf, onebitadder_15_ovf,
       onebitadder_16_ovf, xor_2_out, xor_3_out, xor_4_out, xor_5_out, xor_6_out, xor_7_out, xor_8_out,
       xor_9_out, xor_10_out, xor_11_out, xor_12_out, xor_13_out, xor_14_out, xor_15_out, xor_16_out,
       xor_17_out;
  wire [15:0] not_1_out;

  xor xor_1 (ovf, onebitadder_1_ovf, onebitadder_2_ovf);
  xor xor_2 (xor_2_out, B[14], sub);
  xor xor_3 (xor_3_out, B[15], sub);
  oneBitAdder onebitadder_1 (
    .A(A[15]), .B(xor_3_out), .sub(onebitadder_2_ovf), .ovf(onebitadder_1_ovf), .result(out_7));
  assign not_1_out = ~{out_7, result[14:0]};  // NOT_Gate not_1, 16 bits wide
  xor xor_4 (xor_4_out, B[13], sub);
  oneBitAdder onebitadder_2 (
    .A(A[14]), .B(xor_2_out), .sub(onebitadder_3_ovf), .ovf(onebitadder_2_ovf), .result(result[14]));
  oneBitAdder onebitadder_3 (
    .A(A[13]), .B(xor_4_out), .sub(onebitadder_4_ovf), .ovf(onebitadder_3_ovf), .result(result[13]));
  xor xor_5 (xor_5_out, B[11], sub);
  xor xor_6 (xor_6_out, B[12], sub);
  oneBitAdder onebitadder_4 (
    .A(A[12]), .B(xor_6_out), .sub(onebitadder_6_ovf), .ovf(onebitadder_4_ovf), .result(result[12]));
  xor xor_7 (xor_7_out, B[10], sub);
  oneBitAdder onebitadder_5 (
    .A(A[10]), .B(xor_7_out), .sub(onebitadder_7_ovf), .ovf(onebitadder_5_ovf), .result(result[10]));
  oneBitAdder onebitadder_6 (
    .A(A[11]), .B(xor_5_out), .sub(onebitadder_5_ovf), .ovf(onebitadder_6_ovf), .result(result[11]));
  xor xor_8 (xor_8_out, B[9], sub);
  xor xor_9 (xor_9_out, B[8], sub);
  oneBitAdder onebitadder_7 (
    .A(A[9]), .B(xor_8_out), .sub(onebitadder_8_ovf), .ovf(onebitadder_7_ovf), .result(result[9]));
  oneBitAdder onebitadder_8 (
    .A(A[8]), .B(xor_9_out), .sub(onebitadder_9_ovf), .ovf(onebitadder_8_ovf), .result(result[8]));
  and and_1 (zero, not_1_out[0], not_1_out[1], not_1_out[2], not_1_out[3], not_1_out[4], not_1_out[5], not_1_out[6], not_1_out[7], not_1_out[8], not_1_out[9], not_1_out[10], not_1_out[11], not_1_out[12], not_1_out[13], not_1_out[14], not_1_out[15]);
  xor xor_10 (xor_10_out, B[7], sub);
  xor xor_11 (xor_11_out, B[6], sub);
  oneBitAdder onebitadder_9 (
    .A(A[7]), .B(xor_10_out), .sub(onebitadder_10_ovf), .ovf(onebitadder_9_ovf), .result(result[7]));
  xor xor_12 (xor_12_out, B[5], sub);
  oneBitAdder onebitadder_10 (
    .A(A[6]), .B(xor_11_out), .sub(onebitadder_11_ovf), .ovf(onebitadder_10_ovf), .result(result[6]));
  oneBitAdder onebitadder_11 (
    .A(A[5]), .B(xor_12_out), .sub(onebitadder_12_ovf), .ovf(onebitadder_11_ovf), .result(result[5]));
  xor xor_13 (xor_13_out, B[3], sub);
  xor xor_14 (xor_14_out, B[4], sub);
  oneBitAdder onebitadder_12 (
    .A(A[4]), .B(xor_14_out), .sub(onebitadder_13_ovf), .ovf(onebitadder_12_ovf), .result(result[4]));
  oneBitAdder onebitadder_13 (
    .A(A[3]), .B(xor_13_out), .sub(onebitadder_14_ovf), .ovf(onebitadder_13_ovf), .result(result[3]));
  xor xor_15 (xor_15_out, B[2], sub);
  oneBitAdder onebitadder_14 (
    .A(A[2]), .B(xor_15_out), .sub(onebitadder_16_ovf), .ovf(onebitadder_14_ovf), .result(result[2]));
  xor xor_16 (xor_16_out, B[1], sub);
  xor xor_17 (xor_17_out, B[0], sub);
  oneBitAdder onebitadder_15 (.A(A[0]), .B(xor_17_out), .sub(sub), .ovf(onebitadder_15_ovf), .result(result[0]));
  oneBitAdder onebitadder_16 (
    .A(A[1]), .B(xor_16_out), .sub(onebitadder_15_ovf), .ovf(onebitadder_16_ovf), .result(result[1]));

  assign result[15] = out_7;
endmodule

module memory_latch (
  input  [15:0] address,
  input  WE,
  input  clk,
  input  [15:0] data_in,
  output [15:0] address_latched,
  output WE_latched,
  output OE_latched,
  output [15:0] data_in_latched
);

  wire d_ff_1_q;
  wire [15:0] register_1_q;

  Register #(.width(16), .trigger("falling")) register_1 (
    .D(address), .en(WE), .clk(clk), .Q(register_1_q));  // open: clr
  D_Flip_Flop #(.trigger("falling")) d_ff_1 (.D(WE), .clk(clk), .Q(d_ff_1_q));  // open: Qn, preset, reset
  Register #(.width(16), .trigger("falling")) register_2 (
    .D(data_in), .en(WE), .clk(clk), .Q(data_in_latched));  // open: clr
  Multiplexer #(.width(16), .enable("false")) multiplexer_1 (
    .in0(address), .in1(register_1_q), .out(address_latched), .sel(d_ff_1_q));
  and and_1 (WE_latched, clk, d_ff_1_q);
  not not_1 (OE_latched, WE_latched);
endmodule

module signExtender (
  input  [5:0] in_1,
  output [15:0] out_2
);


  assign out_2 = {{11{in_1[5]}}, in_1[4:0]};

  // Other names for the same wires on the sheet: bit0 = in_1[0]; bit1 = in_1[1]; bit2 = in_1[2]; bit3 = in_1[3];
  //   bit4 = in_1[4]; bit5 = in_1[5]
endmodule

module jumpExtender (
  input  [3:0] in_1,
  input  [11:0] in_2
);
endmodule

module leftsh1 (
  input  [15:0] in_1,
  input  in_2,
  output [15:0] out_3
);

  Multiplexer #(.enable("false")) multiplexer_1 (.in0(in_1[15]), .in1(in_1[14]), .out(out_3[15]), .sel(in_2));
  Multiplexer #(.enable("false")) multiplexer_2 (.in0(in_1[14]), .in1(in_1[13]), .out(out_3[14]), .sel(in_2));
  Multiplexer #(.enable("false")) multiplexer_3 (.in0(in_1[13]), .in1(in_1[12]), .out(out_3[13]), .sel(in_2));
  Multiplexer #(.enable("false")) multiplexer_4 (.in0(in_1[12]), .in1(in_1[11]), .out(out_3[12]), .sel(in_2));
  Multiplexer #(.enable("false")) multiplexer_5 (.in0(in_1[11]), .in1(in_1[10]), .out(out_3[11]), .sel(in_2));
  Multiplexer #(.enable("false")) multiplexer_6 (.in0(in_1[10]), .in1(in_1[9]), .out(out_3[10]), .sel(in_2));
  Multiplexer #(.enable("false")) multiplexer_7 (.in0(in_1[9]), .in1(in_1[8]), .out(out_3[9]), .sel(in_2));
  Multiplexer #(.enable("false")) multiplexer_8 (.in0(in_1[8]), .in1(in_1[7]), .out(out_3[8]), .sel(in_2));
  Multiplexer #(.enable("false")) multiplexer_9 (.in0(in_1[7]), .in1(in_1[6]), .out(out_3[7]), .sel(in_2));
  Multiplexer #(.enable("false")) multiplexer_10 (.in0(in_1[6]), .in1(in_1[5]), .out(out_3[6]), .sel(in_2));
  Multiplexer #(.enable("false")) multiplexer_11 (.in0(in_1[5]), .in1(in_1[4]), .out(out_3[5]), .sel(in_2));
  Multiplexer #(.enable("false")) multiplexer_12 (.in0(in_1[4]), .in1(in_1[3]), .out(out_3[4]), .sel(in_2));
  Multiplexer #(.enable("false")) multiplexer_13 (.in0(in_1[3]), .in1(in_1[2]), .out(out_3[3]), .sel(in_2));
  Multiplexer #(.enable("false")) multiplexer_14 (.in0(in_1[2]), .in1(in_1[1]), .out(out_3[2]), .sel(in_2));
  Multiplexer #(.enable("false")) multiplexer_15 (.in0(in_1[1]), .in1(in_1[0]), .out(out_3[1]), .sel(in_2));
  Multiplexer #(.enable("false")) multiplexer_16 (.in0(in_1[0]), .in1(1'b0), .out(out_3[0]), .sel(in_2));

  // Other names for the same wires on the sheet: bit0 = in_1[0]; bit1 = in_1[1]; bit2 = in_1[2]; bit3 = in_1[3];
  //   bit4 = in_1[4]; bit5 = in_1[5]; bit6 = in_1[6]; bit7 = in_1[7]; bit8 = in_1[8]; bit9 = in_1[9];
  //   bit10 = in_1[10]; bit11 = in_1[11]; bit12 = in_1[12]; bit13 = in_1[13]; bit14 = in_1[14]; bit15 = in_1[15];
  //   out0 = out_3[0]; out1 = out_3[1]; out2 = out_3[2]; out3 = out_3[3]; out4 = out_3[4]; out5 = out_3[5];
  //   out6 = out_3[6]; out7 = out_3[7]; out8 = out_3[8]; out9 = out_3[9]; out10 = out_3[10]; out11 = out_3[11];
  //   out12 = out_3[12]; out13 = out_3[13]; out14 = out_3[14]; out15 = out_3[15]; selectShift = in_2
endmodule

module leftsh2 (
  input  [15:0] in_1,
  input  in_2,
  output [15:0] out_3
);

  Multiplexer #(.enable("false")) multiplexer_1 (.in0(in_1[15]), .in1(in_1[13]), .out(out_3[15]), .sel(in_2));
  Multiplexer #(.enable("false")) multiplexer_2 (.in0(in_1[14]), .in1(in_1[12]), .out(out_3[14]), .sel(in_2));
  Multiplexer #(.enable("false")) multiplexer_3 (.in0(in_1[13]), .in1(in_1[11]), .out(out_3[13]), .sel(in_2));
  Multiplexer #(.enable("false")) multiplexer_4 (.in0(in_1[12]), .in1(in_1[10]), .out(out_3[12]), .sel(in_2));
  Multiplexer #(.enable("false")) multiplexer_5 (.in0(in_1[11]), .in1(in_1[9]), .out(out_3[11]), .sel(in_2));
  Multiplexer #(.enable("false")) multiplexer_6 (.in0(in_1[10]), .in1(in_1[8]), .out(out_3[10]), .sel(in_2));
  Multiplexer #(.enable("false")) multiplexer_7 (.in0(in_1[9]), .in1(in_1[7]), .out(out_3[9]), .sel(in_2));
  Multiplexer #(.enable("false")) multiplexer_8 (.in0(in_1[8]), .in1(in_1[6]), .out(out_3[8]), .sel(in_2));
  Multiplexer #(.enable("false")) multiplexer_9 (.in0(in_1[7]), .in1(in_1[5]), .out(out_3[7]), .sel(in_2));
  Multiplexer #(.enable("false")) multiplexer_10 (.in0(in_1[6]), .in1(in_1[4]), .out(out_3[6]), .sel(in_2));
  Multiplexer #(.enable("false")) multiplexer_11 (.in0(in_1[5]), .in1(in_1[3]), .out(out_3[5]), .sel(in_2));
  Multiplexer #(.enable("false")) multiplexer_12 (.in0(in_1[4]), .in1(in_1[2]), .out(out_3[4]), .sel(in_2));
  Multiplexer #(.enable("false")) multiplexer_13 (.in0(in_1[3]), .in1(in_1[1]), .out(out_3[3]), .sel(in_2));
  Multiplexer #(.enable("false")) multiplexer_14 (.in0(in_1[2]), .in1(in_1[0]), .out(out_3[2]), .sel(in_2));
  Multiplexer #(.enable("false")) multiplexer_15 (.in0(in_1[1]), .in1(1'b0), .out(out_3[1]), .sel(in_2));
  Multiplexer #(.enable("false")) multiplexer_16 (.in0(in_1[0]), .in1(1'b0), .out(out_3[0]), .sel(in_2));

  // Other names for the same wires on the sheet: bit0 = in_1[0]; bit1 = in_1[1]; bit2 = in_1[2]; bit3 = in_1[3];
  //   bit4 = in_1[4]; bit5 = in_1[5]; bit6 = in_1[6]; bit7 = in_1[7]; bit8 = in_1[8]; bit9 = in_1[9];
  //   bit10 = in_1[10]; bit11 = in_1[11]; bit12 = in_1[12]; bit13 = in_1[13]; bit14 = in_1[14]; bit15 = in_1[15];
  //   out0 = out_3[0]; out1 = out_3[1]; out2 = out_3[2]; out3 = out_3[3]; out4 = out_3[4]; out5 = out_3[5];
  //   out6 = out_3[6]; out7 = out_3[7]; out8 = out_3[8]; out9 = out_3[9]; out10 = out_3[10]; out11 = out_3[11];
  //   out12 = out_3[12]; out13 = out_3[13]; out14 = out_3[14]; out15 = out_3[15]; selectShift = in_2
endmodule

module leftsh4 (
  input  [15:0] in_1,
  input  in_2,
  output [15:0] out_3
);

  Multiplexer #(.enable("false")) multiplexer_1 (.in0(in_1[15]), .in1(in_1[11]), .out(out_3[15]), .sel(in_2));
  Multiplexer #(.enable("false")) multiplexer_2 (.in0(in_1[14]), .in1(in_1[6]), .out(out_3[14]), .sel(in_2));
  Multiplexer #(.enable("false")) multiplexer_3 (.in0(in_1[13]), .in1(in_1[9]), .out(out_3[13]), .sel(in_2));
  Multiplexer #(.enable("false")) multiplexer_4 (.in0(in_1[12]), .in1(in_1[8]), .out(out_3[12]), .sel(in_2));
  Multiplexer #(.enable("false")) multiplexer_5 (.in0(in_1[11]), .in1(in_1[7]), .out(out_3[11]), .sel(in_2));
  Multiplexer #(.enable("false")) multiplexer_6 (.in0(in_1[10]), .in1(in_1[6]), .out(out_3[10]), .sel(in_2));
  Multiplexer #(.enable("false")) multiplexer_7 (.in0(in_1[9]), .in1(in_1[5]), .out(out_3[9]), .sel(in_2));
  Multiplexer #(.enable("false")) multiplexer_8 (.in0(in_1[8]), .in1(in_1[4]), .out(out_3[8]), .sel(in_2));
  Multiplexer #(.enable("false")) multiplexer_9 (.in0(in_1[7]), .in1(in_1[3]), .out(out_3[7]), .sel(in_2));
  Multiplexer #(.enable("false")) multiplexer_10 (.in0(in_1[6]), .in1(in_1[2]), .out(out_3[6]), .sel(in_2));
  Multiplexer #(.enable("false")) multiplexer_11 (.in0(in_1[5]), .in1(in_1[1]), .out(out_3[5]), .sel(in_2));
  Multiplexer #(.enable("false")) multiplexer_12 (.in0(in_1[4]), .in1(in_1[0]), .out(out_3[4]), .sel(in_2));
  Multiplexer #(.enable("false")) multiplexer_13 (.in0(in_1[3]), .in1(1'b0), .out(out_3[3]), .sel(in_2));
  Multiplexer #(.enable("false")) multiplexer_14 (.in0(in_1[2]), .in1(1'b0), .out(out_3[2]), .sel(in_2));
  Multiplexer #(.enable("false")) multiplexer_15 (.in0(in_1[1]), .in1(1'b0), .out(out_3[1]), .sel(in_2));
  Multiplexer #(.enable("false")) multiplexer_16 (.in0(in_1[0]), .in1(1'b0), .out(out_3[0]), .sel(in_2));

  // Other names for the same wires on the sheet: bit0 = in_1[0]; bit1 = in_1[1]; bit2 = in_1[2]; bit3 = in_1[3];
  //   bit4 = in_1[4]; bit5 = in_1[5]; bit6 = in_1[6]; bit7 = in_1[7]; bit8 = in_1[8]; bit9 = in_1[9];
  //   bit10 = in_1[10]; bit11 = in_1[11]; bit12 = in_1[12]; bit13 = in_1[13]; bit14 = in_1[14]; bit15 = in_1[15];
  //   out0 = out_3[0]; out1 = out_3[1]; out2 = out_3[2]; out3 = out_3[3]; out4 = out_3[4]; out5 = out_3[5];
  //   out6 = out_3[6]; out7 = out_3[7]; out8 = out_3[8]; out9 = out_3[9]; out10 = out_3[10]; out11 = out_3[11];
  //   out12 = out_3[12]; out13 = out_3[13]; out14 = out_3[14]; out15 = out_3[15]; selectShift = in_2
endmodule

module leftBarrelshifter (
  input  [2:0] shiftBits,
  input  [15:0] in_2,
  output [15:0] out_3
);

  wire [15:0] leftsh1_1_out_3, leftsh2_1_out_3;

  leftsh1 leftsh1_1 (.in_1(in_2), .in_2(shiftBits[0]), .out_3(leftsh1_1_out_3));
  leftsh2 leftsh2_1 (.in_1(leftsh1_1_out_3), .in_2(shiftBits[1]), .out_3(leftsh2_1_out_3));
  leftsh4 leftsh4_1 (.in_1(leftsh2_1_out_3), .in_2(shiftBits[2]), .out_3(out_3));

  // Other names for the same wires on the sheet: sh0 = shiftBits[0]; sh1 = shiftBits[1]; sh2 = shiftBits[2]
endmodule

module rightsh1 (
  input  [15:0] in_1,
  input  in_2,
  output [15:0] out_3
);

  Multiplexer #(.enable("false")) multiplexer_1 (.in0(in_1[0]), .in1(in_1[1]), .out(out_3[0]), .sel(in_2));
  Multiplexer #(.enable("false")) multiplexer_2 (.in0(in_1[1]), .in1(in_1[2]), .out(out_3[1]), .sel(in_2));
  Multiplexer #(.enable("false")) multiplexer_3 (.in0(in_1[2]), .in1(in_1[3]), .out(out_3[2]), .sel(in_2));
  Multiplexer #(.enable("false")) multiplexer_4 (.in0(in_1[3]), .in1(in_1[4]), .out(out_3[3]), .sel(in_2));
  Multiplexer #(.enable("false")) multiplexer_5 (.in0(in_1[4]), .in1(in_1[5]), .out(out_3[4]), .sel(in_2));
  Multiplexer #(.enable("false")) multiplexer_6 (.in0(in_1[5]), .in1(in_1[6]), .out(out_3[5]), .sel(in_2));
  Multiplexer #(.enable("false")) multiplexer_7 (.in0(in_1[6]), .in1(in_1[7]), .out(out_3[6]), .sel(in_2));
  Multiplexer #(.enable("false")) multiplexer_8 (.in0(in_1[7]), .in1(in_1[8]), .out(out_3[7]), .sel(in_2));
  Multiplexer #(.enable("false")) multiplexer_9 (.in0(in_1[8]), .in1(in_1[9]), .out(out_3[8]), .sel(in_2));
  Multiplexer #(.enable("false")) multiplexer_10 (.in0(in_1[9]), .in1(in_1[10]), .out(out_3[9]), .sel(in_2));
  Multiplexer #(.enable("false")) multiplexer_11 (.in0(in_1[10]), .in1(in_1[11]), .out(out_3[10]), .sel(in_2));
  Multiplexer #(.enable("false")) multiplexer_12 (.in0(in_1[11]), .in1(in_1[12]), .out(out_3[11]), .sel(in_2));
  Multiplexer #(.enable("false")) multiplexer_13 (.in0(in_1[12]), .in1(in_1[13]), .out(out_3[12]), .sel(in_2));
  Multiplexer #(.enable("false")) multiplexer_14 (.in0(in_1[13]), .in1(in_1[14]), .out(out_3[13]), .sel(in_2));
  Multiplexer #(.enable("false")) multiplexer_15 (.in0(in_1[14]), .in1(in_1[15]), .out(out_3[14]), .sel(in_2));
  Multiplexer #(.enable("false")) multiplexer_16 (.in0(in_1[15]), .in1(1'b0), .out(out_3[15]), .sel(in_2));

  // Other names for the same wires on the sheet: bit0 = in_1[0]; bit1 = in_1[1]; bit2 = in_1[2]; bit3 = in_1[3];
  //   bit4 = in_1[4]; bit5 = in_1[5]; bit6 = in_1[6]; bit7 = in_1[7]; bit8 = in_1[8]; bit9 = in_1[9];
  //   bit10 = in_1[10]; bit11 = in_1[11]; bit12 = in_1[12]; bit13 = in_1[13]; bit14 = in_1[14]; bit15 = in_1[15];
  //   out0 = out_3[0]; out1 = out_3[1]; out2 = out_3[2]; out3 = out_3[3]; out4 = out_3[4]; out5 = out_3[5];
  //   out6 = out_3[6]; out7 = out_3[7]; out8 = out_3[8]; out9 = out_3[9]; out10 = out_3[10]; out11 = out_3[11];
  //   out12 = out_3[12]; out13 = out_3[13]; out14 = out_3[14]; out15 = out_3[15]; selectShift = in_2
endmodule

module rightsh2 (
  input  [15:0] in_1,
  input  in_2,
  output [15:0] out_3
);

  Multiplexer #(.enable("false")) multiplexer_1 (.in0(in_1[0]), .in1(in_1[2]), .out(out_3[0]), .sel(in_2));
  Multiplexer #(.enable("false")) multiplexer_2 (.in0(in_1[1]), .in1(in_1[3]), .out(out_3[1]), .sel(in_2));
  Multiplexer #(.enable("false")) multiplexer_3 (.in0(in_1[2]), .in1(in_1[4]), .out(out_3[2]), .sel(in_2));
  Multiplexer #(.enable("false")) multiplexer_4 (.in0(in_1[3]), .in1(in_1[5]), .out(out_3[3]), .sel(in_2));
  Multiplexer #(.enable("false")) multiplexer_5 (.in0(in_1[4]), .in1(in_1[6]), .out(out_3[4]), .sel(in_2));
  Multiplexer #(.enable("false")) multiplexer_6 (.in0(in_1[5]), .in1(in_1[7]), .out(out_3[5]), .sel(in_2));
  Multiplexer #(.enable("false")) multiplexer_7 (.in0(in_1[6]), .in1(in_1[8]), .out(out_3[6]), .sel(in_2));
  Multiplexer #(.enable("false")) multiplexer_8 (.in0(in_1[7]), .in1(in_1[9]), .out(out_3[7]), .sel(in_2));
  Multiplexer #(.enable("false")) multiplexer_9 (.in0(in_1[8]), .in1(in_1[10]), .out(out_3[8]), .sel(in_2));
  Multiplexer #(.enable("false")) multiplexer_10 (.in0(in_1[9]), .in1(in_1[11]), .out(out_3[9]), .sel(in_2));
  Multiplexer #(.enable("false")) multiplexer_11 (.in0(in_1[10]), .in1(in_1[12]), .out(out_3[10]), .sel(in_2));
  Multiplexer #(.enable("false")) multiplexer_12 (.in0(in_1[11]), .in1(in_1[13]), .out(out_3[11]), .sel(in_2));
  Multiplexer #(.enable("false")) multiplexer_13 (.in0(in_1[12]), .in1(in_1[14]), .out(out_3[12]), .sel(in_2));
  Multiplexer #(.enable("false")) multiplexer_14 (.in0(in_1[13]), .in1(in_1[15]), .out(out_3[13]), .sel(in_2));
  Multiplexer #(.enable("false")) multiplexer_15 (.in0(in_1[14]), .in1(1'b0), .out(out_3[14]), .sel(in_2));
  Multiplexer #(.enable("false")) multiplexer_16 (.in0(in_1[15]), .in1(1'b0), .out(out_3[15]), .sel(in_2));

  // Other names for the same wires on the sheet: bit0 = in_1[0]; bit1 = in_1[1]; bit2 = in_1[2]; bit3 = in_1[3];
  //   bit4 = in_1[4]; bit5 = in_1[5]; bit6 = in_1[6]; bit7 = in_1[7]; bit8 = in_1[8]; bit9 = in_1[9];
  //   bit10 = in_1[10]; bit11 = in_1[11]; bit12 = in_1[12]; bit13 = in_1[13]; bit14 = in_1[14]; bit15 = in_1[15];
  //   out0 = out_3[0]; out1 = out_3[1]; out2 = out_3[2]; out3 = out_3[3]; out4 = out_3[4]; out5 = out_3[5];
  //   out6 = out_3[6]; out7 = out_3[7]; out8 = out_3[8]; out9 = out_3[9]; out10 = out_3[10]; out11 = out_3[11];
  //   out12 = out_3[12]; out13 = out_3[13]; out14 = out_3[14]; out15 = out_3[15]; selectShift = in_2
endmodule

module rightsh4 (
  input  [15:0] in_1,
  input  in_2,
  output [15:0] out_3
);

  Multiplexer #(.enable("false")) multiplexer_1 (.in0(in_1[0]), .in1(in_1[4]), .out(out_3[0]), .sel(in_2));
  Multiplexer #(.enable("false")) multiplexer_2 (.in0(in_1[1]), .in1(in_1[5]), .out(out_3[1]), .sel(in_2));
  Multiplexer #(.enable("false")) multiplexer_3 (.in0(in_1[2]), .in1(in_1[6]), .out(out_3[2]), .sel(in_2));
  Multiplexer #(.enable("false")) multiplexer_4 (.in0(in_1[3]), .in1(in_1[7]), .out(out_3[3]), .sel(in_2));
  Multiplexer #(.enable("false")) multiplexer_5 (.in0(in_1[4]), .in1(in_1[8]), .out(out_3[4]), .sel(in_2));
  Multiplexer #(.enable("false")) multiplexer_6 (.in0(in_1[5]), .in1(in_1[9]), .out(out_3[5]), .sel(in_2));
  Multiplexer #(.enable("false")) multiplexer_7 (.in0(in_1[6]), .in1(in_1[10]), .out(out_3[6]), .sel(in_2));
  Multiplexer #(.enable("false")) multiplexer_8 (.in0(in_1[7]), .in1(in_1[11]), .out(out_3[7]), .sel(in_2));
  Multiplexer #(.enable("false")) multiplexer_9 (.in0(in_1[8]), .in1(in_1[12]), .out(out_3[8]), .sel(in_2));
  Multiplexer #(.enable("false")) multiplexer_10 (.in0(in_1[9]), .in1(in_1[13]), .out(out_3[9]), .sel(in_2));
  Multiplexer #(.enable("false")) multiplexer_11 (.in0(in_1[10]), .in1(in_1[14]), .out(out_3[10]), .sel(in_2));
  Multiplexer #(.enable("false")) multiplexer_12 (.in0(in_1[11]), .in1(in_1[15]), .out(out_3[11]), .sel(in_2));
  Multiplexer #(.enable("false")) multiplexer_13 (.in0(in_1[12]), .in1(1'b0), .out(out_3[12]), .sel(in_2));
  Multiplexer #(.enable("false")) multiplexer_14 (.in0(in_1[13]), .in1(1'b0), .out(out_3[13]), .sel(in_2));
  Multiplexer #(.enable("false")) multiplexer_15 (.in0(in_1[14]), .in1(1'b0), .out(out_3[14]), .sel(in_2));
  Multiplexer #(.enable("false")) multiplexer_16 (.in0(in_1[15]), .in1(1'b0), .out(out_3[15]), .sel(in_2));

  // Other names for the same wires on the sheet: bit0 = in_1[0]; bit1 = in_1[1]; bit2 = in_1[2]; bit3 = in_1[3];
  //   bit4 = in_1[4]; bit5 = in_1[5]; bit6 = in_1[6]; bit7 = in_1[7]; bit8 = in_1[8]; bit9 = in_1[9];
  //   bit10 = in_1[10]; bit11 = in_1[11]; bit12 = in_1[12]; bit13 = in_1[13]; bit14 = in_1[14]; bit15 = in_1[15];
  //   out0 = out_3[0]; out1 = out_3[1]; out2 = out_3[2]; out3 = out_3[3]; out4 = out_3[4]; out5 = out_3[5];
  //   out6 = out_3[6]; out7 = out_3[7]; out8 = out_3[8]; out9 = out_3[9]; out10 = out_3[10]; out11 = out_3[11];
  //   out12 = out_3[12]; out13 = out_3[13]; out14 = out_3[14]; out15 = out_3[15]; selectShift = in_2
endmodule

module rightBarrelshifter (
  input  [2:0] shiftBits,
  input  [15:0] in_2,
  output [15:0] out_3
);

  wire [15:0] rightsh1_1_out_3, rightsh2_1_out_3;

  rightsh1 rightsh1_1 (.in_1(in_2), .in_2(shiftBits[0]), .out_3(rightsh1_1_out_3));
  rightsh2 rightsh2_1 (.in_1(rightsh1_1_out_3), .in_2(shiftBits[1]), .out_3(rightsh2_1_out_3));
  rightsh4 rightsh4_1 (.in_1(rightsh2_1_out_3), .in_2(shiftBits[2]), .out_3(out_3));

  // Other names for the same wires on the sheet: sh0 = shiftBits[0]; sh1 = shiftBits[1]; sh2 = shiftBits[2]
endmodule
